# Fritzing sketch Wiring (saved by Fritzing 0.9.3b)

parts:
  Part1 = Arduino Nano (Rev3.0)
  Part3 = Adafruit 2.4in TFT FeatherWing [part_number="Adafruit #3315"]
  Part4 = Adafruit TSL2591 [part_number="Adafruit #1980"]
  Part5 = PowerBoost 500 Charger
  BATT1 = LiPoly Battery (1300mAh)

nets:
  N1: Part1.D8, Part3.EN
  N2: Part1.D9, Part3.K
  N3: Part1.D10, Part3.J
  N4: Part1.D11/MOSI, Part3.MOSI
  N5: Part1.D12/MISO, Part3.MISO
  N6: Part1.VIN, Part5.5.0V
  GND: Part1.GND, Part4.GND
  5V: Part1.5V, Part4.VIN
  N7: Part1.A5, Part4.SCL
  N8: Part1.A4, Part4.SDA
  N9: Part1.D13/SCK, Part3.SCLK
  N10: Part5.GND, BATT1.negative
  N11: Part5.VBAT, BATT1.positive

custom parts:
  Adafruit 2.4in TFT FeatherWing: Spice up your Feather project with a beautiful 2.4" touchscreen display shield with built in microSD card socket. This TFT display is 2.4" diagonal with a bright 4 white-LED backlight. You get 240x320 pixels with individual 16-bit color pixel control. It has way more resolution than a black and white 128x64 display. As a bonus, this display comes with a resistive touchscreen attached to it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
  Adafruit TSL2591: When the future is dazzlingly-bright, this ultra-high-range luminosity sensor will help you measure it. The TSL2591 luminosity sensor is an advanced digital light sensor, ideal for use in a wide range of light situations. Compared to low cost CdS cells, this sensor is more precise, allowing for exact lux calculations and can be configured for different gain/timing ranges to detect light ranges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
  PowerBoost 500 Charger: The PowerBoost 500C is a little DC/DC boost converter module that can be powered by any 3.7V LiIon/LiPoly battery, and convert the battery output to 5.2V DC for running your 5V projects. At its heart is a TPS61090 boost converter from TI. This boost converter chip has some really nice extras such as low battery detection, 2A internal switch, synchronous conversion, excellent efficiency, and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
  LiPoly Battery (1300mAh): Lithium Ion Polymer Battery (1300mAh)
